# Fritzing sketch carsensor (saved by Fritzing 0.8.3b)
breadboards: 1

parts:
  Part1 = Arduino Micro (Rev3)
  U1 = mystery part, 9 pins [chip_label="New Way BFD-1000"]

nets:
  N1: Part1.5V, U1.pin2
  N2: Part1.GND, U1.pin9
  N3: Part1.D3/SCL, U1.pin3
  N4: Part1.D4_PWM/A6, U1.pin4
  N5: Part1.D5_PWM, U1.pin5
  N6: Part1.D6_PWM/A7, U1.pin6
  N7: Part1.D7, U1.pin7
