# Fritzing sketch robot-car (saved by Fritzing 0.8.3b)
breadboards: 3

parts:
  Part3 = Arduino Nano (Rev3.0)
  Part4 = Arduino Nano (Rev3.0)
  U3 = mystery part, 9 pins [chip_label="New Way BFD-1000"]
  VCC1 = Battery block 9V
  IC3 = RX-2B [package=dip16]
  VCC2 = 4 x AAA Battery Mount
  R4 = Resistor [tolerance=±5% resistance=10k package=THT]

nets:
  GND: Part3.GND, Part4.GND, U3.pin9, VCC1.-, IC3.GND, VCC2.-, R4.Pin_0
  N1: Part3.D8, IC3.SI, R4.Pin_1
  N2: Part3.D11/MOSI, Part4.D11/MOSI
  N3: Part3.D12/MISO, Part4.D12/MISO
  VIN: Part3.VIN, Part3.5V, Part4.VIN, Part4.5V, U3.pin2, VCC1.+
  N4: Part4.D4, U3.pin3
  N5: Part4.D5, U3.pin4
  N6: Part4.D6, U3.pin5
  N7: Part4.D7, U3.pin6
  N8: Part4.D8, U3.pin7
  N9: IC3.VDD, VCC2.+

notes:
  Sensor controller
  Motorr controller
  Car control module
  Line hunting sensor

custom parts:
  RX-2B: The TX-2B/RX-2B is a pair of CMOS LSIs designed for remote controlled car applications. The TX-2B/RX-2B has five control keys for controlling the motions (i.e. forward, backward, rightward, leftward and the turbo function) of the remote controlled car.
