# Fritzing sketch arduino_to_rx2b (saved by Fritzing 0.8.3b)
breadboards: 1

parts:
  Part1 = Arduino Mega 2560 (Rev3)
  R1 = Resistor [tolerance=±5% resistance=1k package=THT]
  R2 = Resistor [tolerance=±5% resistance=10k package=THT]
  IC1 = RX-2B [package=dip16]

nets:
  N1: Part1.D11_PWM, R1.Pin_0
  GND: Part1.GND, R2.Pin_0, IC1.GND
  N2: R1.Pin_1, R2.Pin_1, IC1.SI

custom parts:
  RX-2B: The TX-2B/RX-2B is a pair of CMOS LSIs designed for remote controlled car applications. The TX-2B/RX-2B has five control keys for controlling the motions (i.e. forward, backward, rightward, leftward and the turbo function) of the remote controlled car.
